# Fritzing sketch heating-element-and-relay-wiring (saved by Fritzing 0.9.3b)
breadboards: 1

parts:
  JACK1 = 2.1mm Barrel Jack with Terminal Block
  J1 = T Cobbler Plus
  Raspberry_Pi_1 = Raspberry Pi 4 [part_number=RPI-4-b]
  R1 = Heating Pad
  U1 = 2-Channel 5v Relay Shield [package=relay-2ch5v10a]

nets:
  N1: JACK1.POS, U1.K2-On
  N2: JACK1.NEG, R1.pin_0
  N3: J1.5.0V#1, U1.VCC
  N4: J1.#12, U1.IN1
  N5: J1.GND#33, U1.GND
  3V3: J1.3.3V#41, J1.3.3V#57, Raspberry_Pi_1.3v3, Raspberry_Pi_1.3V3
  5V: J1.5V, Raspberry_Pi_1.5V
  N6: J1.GPIO_2, Raspberry_Pi_1.GPIO2
  N7: J1.GPIO_3, Raspberry_Pi_1.GPIO3
  N8: J1.GND#46, J1.GND#49, J1.GND#54, J1.GND#60, J1.GND#65, J1.GND#70, J1.GND#74, J1.GND#79, Raspberry_Pi_1.GND
  N9: J1.GPIO_4, Raspberry_Pi_1.GPIO4
  N10: J1.GPIO_14, Raspberry_Pi_1.GPIO14
  N11: J1.GPIO_15, Raspberry_Pi_1.GPIO15
  N12: J1.GPIO_17, Raspberry_Pi_1.GPIO17
  N13: J1.GPIO_18, Raspberry_Pi_1.GPIO18
  N14: J1.GPIO_27, Raspberry_Pi_1.GPIO27
  N15: J1.GPIO_22, Raspberry_Pi_1.GPIO22
  N16: J1.GPIO_23, Raspberry_Pi_1.GPIO23
  N17: J1.GPIO_24, Raspberry_Pi_1.GPIO24
  N18: J1.GPIO_10, Raspberry_Pi_1.GPIO10
  N19: J1.GPIO_9, Raspberry_Pi_1.GPIO9
  N20: J1.GPIO_25, Raspberry_Pi_1.GPIO25
  N21: J1.GPIO_11, Raspberry_Pi_1.GPIO11
  N22: J1.GPIO_8, Raspberry_Pi_1.GPIO8
  N23: J1.GPIO_7, Raspberry_Pi_1.GPIO7
  N24: J1.ID_SD, Raspberry_Pi_1.ID_SD
  N25: J1.ID_SC, Raspberry_Pi_1.ID_SC
  N26: J1.GPIO_5, Raspberry_Pi_1.GPIO5
  N27: J1.GPIO_6, Raspberry_Pi_1.GPIO6
  N28: J1.GPIO_12, Raspberry_Pi_1.GPIO12
  N29: J1.GPIO_13, Raspberry_Pi_1.GPIO13
  N30: J1.GPIO_19, Raspberry_Pi_1.GPIO19
  N31: J1.GPIO_16, Raspberry_Pi_1.GPIO16
  N32: J1.GPIO_26, Raspberry_Pi_1.GPIO26
  N33: J1.GPIO_20, Raspberry_Pi_1.GPIO20
  N34: J1.GPIO_21, Raspberry_Pi_1.GPIO21
  N35: R1.pin_1, U1.K2-In

notes:
  -
  +
  12V adapter
  VCC
  GND
  IN1 (GPIO12)
  COM
  NO
  Heating element
  12V 110*C

custom parts:
  T Cobbler Plus: The T-Cobbler Plus is an add on prototyping board from Adafruit specifically designed for the Raspberry Pi B+ that can break out all those tasty power, GPIO, I2C and SPI pins from the 40-pin header onto a solderless breadboard. This set will make "cobbling together" prototypes with the Pi super easy. The T-Cobbler Plus can plug into any solderless breadboard.
  Raspberry Pi 4: The RPi4, a faster version of the awesome Raspberry Pi 2 B ARM Board with 40 pin gpio. Ready for special Raspberry Pi B+ and RPi2 Hat (Hardware attached (on) top)
  Heating Pad: A thermoresistant material with an embeded conductor that dissipates electrical energy into heat.
  2-Channel 5v Relay Shield: 2 Channel 5v Relay Shield w. 2x SPD-06VDC-SD-C
