# Fritzing sketch limit-switch-wiring (saved by Fritzing 0.9.3b)

parts:
  Raspberry_Pi_1 = Raspberry Pi 4 [part_number=RPI-4-b]
  JL012-13-5_1 = JL012-13-5.2 Lever (Limit) Switch SPDT + NO + NC [part_number=V-156-1C25]

nets:
  N1: Raspberry_Pi_1.GND, JL012-13-5_1.NC
  N2: Raspberry_Pi_1.GPIO23, JL012-13-5_1.NO

notes:
  Raspi 4B and Limit Switch (V-156-1C25)
  COM (Ground)
  NO (GPIO23)
  NC
  Contact with object

custom parts:
  Raspberry Pi 4: The RPi4, a faster version of the awesome Raspberry Pi 2 B ARM Board with 40 pin gpio. Ready for special Raspberry Pi B+ and RPi2 Hat (Hardware attached (on) top)
  JL012-13-5.2 Lever (Limit) Switch SPDT + NO + NC: Micro Switch; Model No.: JL012-13.5-2; Actuator Action: Momentary; Actuator Type: Hinge Lever; Contact Configuration: 1NO, 1NC (SPDT) Temperature -25~65℃；Relative humidity: below 85%; Rate Voltage: 125V AC; Rated Current: 1A.
