# Fritzing sketch led-panel-wiring (saved by Fritzing 0.9.3b)
breadboards: 1

parts:
  Raspberry_Pi_1 = Raspberry Pi 4 [part_number=RPI-4-b]
  LED1 = smd LED [color="Green (555nm)" package="0805 [SMD]"]
  LED2 = smd LED [color="Red (633nm)" package="0805 [SMD]"]
  LED3 = smd LED [color="White (4500K)" package="0805 [SMD]"]
  LED4 = smd LED [color="Yellow (595nm)" package="0805 [SMD]"]
  LED5 = smd LED [color="White (8000K)" package="0805 [SMD]"]  # not connected
  R1 = Resistor [tolerance=±5% resistance=220 package="2512 [SMD]"]
  R2 = Resistor [tolerance=±5% resistance=220 package="2512 [SMD]"]
  R3 = Resistor [tolerance=±5% resistance=220 package="2512 [SMD]"]
  R4 = Resistor [tolerance=±5% resistance=220 package="2512 [SMD]"]
  R5 = Resistor [tolerance=±5% resistance=220 package="2512 [SMD]"]

nets:
  N1: Raspberry_Pi_1.GPIO17, R5.Pin_0
  N2: Raspberry_Pi_1.GPIO27, R4.Pin_0
  N3: Raspberry_Pi_1.GPIO22, R3.Pin_0
  N4: Raspberry_Pi_1.GPIO6, R2.Pin_0
  N5: Raspberry_Pi_1.GPIO13, R1.Pin_0
  N6: Raspberry_Pi_1.GND, LED1.cathode, LED2.cathode, LED3.cathode, LED4.cathode
  N7: LED1.anode, R4.Pin_1
  N8: LED2.anode, R5.Pin_1
  N9: LED3.anode, R3.Pin_1
  N10: LED4.anode, R2.Pin_1

notes:
  GND
  GPIO17
  GPIO27
  GPIO22
  GPIO6
  GPIO13

custom parts:
  Raspberry Pi 4: The RPi4, a faster version of the awesome Raspberry Pi 2 B ARM Board with 40 pin gpio. Ready for special Raspberry Pi B+ and RPi2 Hat (Hardware attached (on) top)
