# Fritzing sketch rgb-led-aht20-temp-hum-sensor-wiring (saved by Fritzing 0.9.3b)
breadboards: 1

parts:
  Raspberry_Pi_4_model_B = Raspberry Pi 4 [part_number=RPI-4-b]
  AHT20_sensor = DHT22 Humidity and Temperature Sensor  # not connected
  J1 = T Cobbler Plus

nets (from the schematic view):
  3V3: Raspberry_Pi_4_model_B.3v3, Raspberry_Pi_4_model_B.3V3, J1.3.3V#41, J1.3.3V#57
  N1: Raspberry_Pi_4_model_B.GPIO2, J1.GPIO_2
  N2: Raspberry_Pi_4_model_B.GPIO3, J1.GPIO_3
  N3: Raspberry_Pi_4_model_B.GPIO4, J1.GPIO_4
  N4: Raspberry_Pi_4_model_B.GND, J1.GND#46, J1.GND#49, J1.GND#54, J1.GND#60, J1.GND#65, J1.GND#70, J1.GND#74, J1.GND#79
  N5: Raspberry_Pi_4_model_B.GPIO17, J1.GPIO_17
  N6: Raspberry_Pi_4_model_B.GPIO27, J1.GPIO_27
  N7: Raspberry_Pi_4_model_B.GPIO22, J1.GPIO_22
  N8: Raspberry_Pi_4_model_B.GPIO10, J1.GPIO_10
  N9: Raspberry_Pi_4_model_B.GPIO9, J1.GPIO_9
  N10: Raspberry_Pi_4_model_B.GPIO11, J1.GPIO_11
  N11: Raspberry_Pi_4_model_B.ID_SD, J1.ID_SD
  N12: Raspberry_Pi_4_model_B.GPIO5, J1.GPIO_5
  N13: Raspberry_Pi_4_model_B.GPIO6, J1.GPIO_6
  N14: Raspberry_Pi_4_model_B.GPIO13, J1.GPIO_13
  N15: Raspberry_Pi_4_model_B.GPIO19, J1.GPIO_19
  N16: Raspberry_Pi_4_model_B.GPIO26, J1.GPIO_26
  N17: Raspberry_Pi_4_model_B.GPIO21, J1.GPIO_21
  N18: Raspberry_Pi_4_model_B.GPIO20, J1.GPIO_20
  N19: Raspberry_Pi_4_model_B.GPIO16, J1.GPIO_16
  N20: Raspberry_Pi_4_model_B.GPIO12, J1.GPIO_12
  N21: Raspberry_Pi_4_model_B.ID_SC, J1.ID_SC
  N22: Raspberry_Pi_4_model_B.GPIO7, J1.GPIO_7
  N23: Raspberry_Pi_4_model_B.GPIO8, J1.GPIO_8
  N24: Raspberry_Pi_4_model_B.GPIO25, J1.GPIO_25
  N25: Raspberry_Pi_4_model_B.GPIO24, J1.GPIO_24
  N26: Raspberry_Pi_4_model_B.GPIO23, J1.GPIO_23
  N27: Raspberry_Pi_4_model_B.GPIO18, J1.GPIO_18
  N28: Raspberry_Pi_4_model_B.GPIO15, J1.GPIO_15
  N29: Raspberry_Pi_4_model_B.GPIO14, J1.GPIO_14
  5V: Raspberry_Pi_4_model_B.5V, J1.5V

notes:
  3.3V
  SDA
  SCL
  GND

custom parts:
  Raspberry Pi 4: The RPi4, a faster version of the awesome Raspberry Pi 2 B ARM Board with 40 pin gpio. Ready for special Raspberry Pi B+ and RPi2 Hat (Hardware attached (on) top)
  T Cobbler Plus: The T-Cobbler Plus is an add on prototyping board from Adafruit specifically designed for the Raspberry Pi B+ that can break out all those tasty power, GPIO, I2C and SPI pins from the 40-pin header onto a solderless breadboard. This set will make "cobbling together" prototypes with the Pi super easy. The T-Cobbler Plus can plug into any solderless breadboard.
