# Fritzing sketch ultrasonic-range-sensor-wiring (saved by Fritzing 0.9.3b)
breadboards: 1

parts:
  Raspberry_Pi_1 = Raspberry Pi 4 [part_number=RPI-4-b]
  Part1 = SRF05 Ultrasonic Rangefinder
  R1 = Resistor [tolerance=±5% resistance=1k package="2010 [SMD]"]
  R2 = Resistor [tolerance=±5% resistance=1k package="2010 [SMD]"]

nets:
  N1: Raspberry_Pi_1.GPIO25, R1.Pin_0, R2.Pin_1
  GND: Raspberry_Pi_1.GND, Part1.GND, R2.Pin_0
  N2: Raspberry_Pi_1.GPIO24, Part1.Trig
  5V: Raspberry_Pi_1.5V, Part1.VCC
  N3: Part1.Echo, R1.Pin_1

notes:
  1k Ohm
  2k Ohm
  5V VCC
  Ground
  Trig GPIO24
  Echo GPIO25
  Bridge
  Raspi 4B and Ultrasonic range sensor (HC-SR04)

custom parts:
  Raspberry Pi 4: The RPi4, a faster version of the awesome Raspberry Pi 2 B ARM Board with 40 pin gpio. Ready for special Raspberry Pi B+ and RPi2 Hat (Hardware attached (on) top)
